// Logisim project BB-8.circ as structural Verilog: 5 circuits, main circuit main
module main (
);

  wire ALU_ACC, and_1_out, and_2_out, and_3_out, and_4_out, and_6_out, CLK, clock_1_out, comparator_1_eq,
       comparator_2_eq, comparator_3_eq, comparator_4_eq, comparator_5_eq, comparator_6_eq, comparator_7_eq,
       comparator_8_eq, comparator_9_eq, comparator_10_eq, comparator_12_eq, comparator_13_eq,
       controlled_buffer_12_out, EXT_0, EXT_1, EXT_MEM_CLK, EXT_MEM_PRO, EXT_TEL_CLK, FLG_CAR, FLG_EQU,
       FLG_GRE, FLG_LES, FLG_ZER, IF_RES, INC_PC, key_manager_1_clr, key_manager_1_con, key_manager_1_rd,
       keyboard_1_avail, nand_1_out, NIT, not_1_out, not_2_out, not_3_out, not_4_out, not_6_out, not_7_out,
       not_8_out, not_9_out, not_10_out, not_11_out, or_1_out, or_2_out, or_5_out, or_6_out, or_7_out,
       PC_HI_ACC, PC_LO_ACC, PRT_A_B, PRT_B_B, PRT_C_B, PRT_D_B, pull_resistor_4_node, pull_resistor_5_node,
       pull_resistor_7_node, REG_ALU, REG_DIP, REG_EN, REG_MEM, REG_PC_HI, REG_PC_LO, REG_SHI, regs_1_wrt,
       REQ_IF, RST, SYS, telnet_1_p5, telnet_1_p7, ttl_manager_1_ttl_en, ttl_manager_1_ttl_rst, undriven;
  wire [1:0] PRT_BC_SEL;
  wire [3:0] MCC_OP, multiplexer_2_out, rom_1_data;
  wire [6:0] keyboard_1_data, ttl_manager_1_ttl_dat;
  wire [7:0] ACC, ALU, controlled_buffer_2_out, DIP, dipswitch_1_sw8, dipswitch_2_sw8, EXT_MEM_OPCODE,
       EXT_MEM_OPERAND, EXT_TEL_OPCODE, EXT_TEL_OPERAND, MEM, multiplexer_7_out, multiplexer_8_out,
       multiplexer_9_out, PRT_C, PRT_D, ram_1_dout, ram_2_dout, random_1_out, register_1_q, register_2_q,
       register_3_q, rom_2_data, SHI, telnet_1_p4;
  wire [7:7] PC_HI;
  wire [9:0] counter_1_q, multiplexer_1_out;
  wire [14:0] MEM15;
  wire [15:0] multiplexer_5_out;

  // Probe on multiplexer_1_out
  Multiplexer #(.width(10)) multiplexer_1 (
    .in0({10{1'b1}}), .in1({MEM, 2'b00}), .out(multiplexer_1_out), .sel(not_1_out));
  not not_1 (not_1_out, RST);
  or or_1 (or_1_out, RST, NIT);
  Counter #(.max('h3ff), .width(10)) counter_1 (
    .load(or_1_out), .D(multiplexer_1_out), .count(1'b1), .Q(counter_1_q), .up(1'b1), .clk(CLK));  // open: carry, clr
  ROM #(.addrWidth(10)) rom_1 (.addr(counter_1_q), .data({MCC_OP, rom_1_data}));
  Comparator #(.mode("unsigned"), .width(4)) comparator_1 (
    .a(MCC_OP), .b(4'b0001), .eq(comparator_1_eq));  // open: gt, lt
  and and_1 (and_1_out, rom_1_data[0], rom_1_data[1], rom_1_data[2], rom_1_data[3], MCC_OP[0], MCC_OP[1], MCC_OP[2], MCC_OP[3]);
  Clock clock_1 (.out(clock_1_out));
  Pull_Resistor pull_resistor_1 (.node(CLK));
  assign CLK = or_2_out ? clock_1_out : 1'bz;  // Controlled_Buffer controlled_buffer_1
  or or_2 (or_2_out, nand_1_out, RST);
  nand nand_1 (nand_1_out, comparator_1_eq, SYS);
  or or_3 (NIT, IF_RES, and_1_out);
  Decoder #(.select(4)) decoder_1 (
    .out0(REG_MEM), .out1(PC_HI_ACC), .out2(PC_LO_ACC), .out3(INC_PC), .out4(REG_PC_HI), .out5(REG_PC_LO),
    .out6(REG_DIP), .out7(REG_ALU), .out8(ALU_ACC), .out9(REQ_IF), .out10(PRT_A_B), .out11(REG_SHI),
    .out12(PRT_B_B), .out13(PRT_C_B), .out14(PRT_D_B), .out15(SYS), .sel(rom_1_data));  // open: en
  or or_4 (REG_EN, REG_MEM, REG_PC_HI, REG_PC_LO, REG_DIP, REG_ALU, REG_SHI, PRT_C_B, PRT_D_B);
  assign controlled_buffer_2_out = REG_MEM ? MEM : 8'bz;  // Controlled_Buffer controlled_buffer_2
  assign controlled_buffer_2_out = REG_PC_LO ? MEM15[7:0] : 8'bz;  // Controlled_Buffer controlled_buffer_3
  assign controlled_buffer_2_out = REG_PC_HI ? {PC_HI[7], MEM15[14:8]} : 8'bz;  // Controlled_Buffer controlled_buffer_4
  assign controlled_buffer_2_out = REG_DIP ? DIP : 8'bz;  // Controlled_Buffer controlled_buffer_5
  assign controlled_buffer_2_out = REG_ALU ? ALU : 8'bz;  // Controlled_Buffer controlled_buffer_6
  assign controlled_buffer_2_out = REG_SHI ? SHI : 8'bz;  // Controlled_Buffer controlled_buffer_7
  assign controlled_buffer_2_out = PRT_C_B ? PRT_C : 8'bz;  // Controlled_Buffer controlled_buffer_8
  assign controlled_buffer_2_out = PRT_D_B ? PRT_D : 8'bz;  // Controlled_Buffer controlled_buffer_9
  not not_2 (not_2_out, FLG_ZER);
  not not_3 (not_3_out, FLG_CAR);
  not not_4 (not_4_out, FLG_EQU);
  // Probe on undriven
  DipSwitch dipswitch_1 (
    .sw1(dipswitch_1_sw8[7]), .sw2(dipswitch_1_sw8[6]), .sw3(dipswitch_1_sw8[5]), .sw4(dipswitch_1_sw8[4]),
    .sw5(dipswitch_1_sw8[3]), .sw6(dipswitch_1_sw8[2]), .sw7(dipswitch_1_sw8[1]), .sw8(dipswitch_1_sw8[0]));
  DipSwitch dipswitch_2 (
    .sw1(dipswitch_2_sw8[7]), .sw2(dipswitch_2_sw8[6]), .sw3(dipswitch_2_sw8[5]), .sw4(dipswitch_2_sw8[4]),
    .sw5(dipswitch_2_sw8[3]), .sw6(dipswitch_2_sw8[2]), .sw7(dipswitch_2_sw8[1]), .sw8(dipswitch_2_sw8[0]));
  Pull_Resistor pull_resistor_2 (.node(EXT_0));
  Pull_Resistor pull_resistor_3 (.node(EXT_1));
  Pull_Resistor pull_resistor_4 (.node(pull_resistor_4_node));
  not not_5 (pull_resistor_4_node, EXT_1);
  Multiplexer #(.width(4)) multiplexer_2 (.in0(4'b1110), .in1(MCC_OP), .out(multiplexer_2_out), .sel(not_6_out));
  Pull_Resistor pull_resistor_5 (.node(pull_resistor_5_node));
  Multiplexer #(.select(4)) multiplexer_3 (
    .in0(1'b1), .in1(1'b0), .in2(FLG_ZER), .in3(FLG_CAR), .in4(not_2_out), .in5(not_3_out), .in6(FLG_GRE),
    .in7(FLG_EQU), .in8(FLG_LES), .in9(not_4_out), .in10(EXT_0), .in11(EXT_1), .in12(pull_resistor_4_node),
    .out(pull_resistor_5_node), .sel(MCC_OP));  // open: in13, in14, in15
  not not_6 (not_6_out, or_5_out);
  or or_5 (or_5_out, REG_PC_LO, REG_ALU, REG_SHI, REG_PC_HI, REG_DIP, PRT_C_B, PRT_D_B);
  Pull_Resistor pull_resistor_6 (.node(IF_RES));
  not not_7 (not_7_out, pull_resistor_5_node);
  assign IF_RES = REQ_IF ? not_7_out : 1'bz;  // Controlled_Buffer controlled_buffer_10
  // Probe on ALU
  alu_flags alu_flags_1 (
    .CLK(CLK), .EN(ALU_ACC), .INP(ACC), .SEL(MCC_OP), .SHI(SHI), .GRE(FLG_GRE), .EQU(FLG_EQU), .LES(FLG_LES),
    .ZER(FLG_ZER), .RES(ALU), .CAR(FLG_CAR));
  Multiplexer #(.select(4), .width(8)) multiplexer_4 (
    .in0(dipswitch_1_sw8), .in1(dipswitch_2_sw8), .out(DIP), .sel(MCC_OP));  // open: in2, in3, in4, in5, in6, in7, in8, in9, in10, in11, in12, in13, in14, in15
  Comparator #(.mode("unsigned"), .width(2)) comparator_2 (
    .a(2'b00), .b(PRT_BC_SEL), .eq(comparator_2_eq));  // open: gt, lt
  regs regs_1 (
    .EN(REG_EN), .CLK(CLK), .VAL(controlled_buffer_2_out), .RGS(multiplexer_2_out), .WRT(regs_1_wrt),
    .REGA(ACC));
  // Probe on ACC
  Pull_Resistor pull_resistor_7 (.node(pull_resistor_7_node));
  assign pull_resistor_7_node = comparator_2_eq ? CLK : 1'bz;  // Controlled_Buffer controlled_buffer_11
  assign controlled_buffer_12_out = comparator_3_eq ? CLK : 1'bz;  // Controlled_Buffer controlled_buffer_12
  Comparator #(.mode("unsigned"), .width(2)) comparator_3 (
    .a(2'b01), .b(PRT_BC_SEL), .eq(comparator_3_eq));  // open: gt, lt
  // Shift_Register #(.length(2), .width(8)) shift_register_1: pin names not known; wires that end beside it: PRT_B_B, pull_resistor_7_node, ACC, EXT_MEM_OPERAND, EXT_MEM_OPCODE
  and and_2 (and_2_out, comparator_2_eq, PRT_B_B);
  // Shift_Register #(.length(2), .width(8)) shift_register_2: pin names not known; wires that end beside it: PRT_B_B, controlled_buffer_12_out, ACC, EXT_TEL_OPERAND, EXT_TEL_OPCODE
  Pull_Resistor pull_resistor_8 (.node(controlled_buffer_12_out));
  T_Flip_Flop t_ff_1 (.T(and_3_out), .clk(CLK), .Qn(EXT_TEL_CLK));  // open: Q, reset, preset
  and and_3 (and_3_out, comparator_3_eq, PRT_B_B);
  T_Flip_Flop t_ff_2 (.T(and_2_out), .clk(CLK), .Qn(EXT_MEM_CLK));  // open: Q, reset, preset
  RAM #(.addrWidth(15), .asyncread("true")) ram_1 (
    .addr(MEM15), .we(and_4_out), .oe(PC_HI[7]), .clk(and_4_out), .din(ACC), .dout(ram_1_dout));
  and and_4 (and_4_out, PC_HI[7], regs_1_wrt);
  not not_8 (not_8_out, CLK);
  and and_5 (EXT_MEM_PRO, not_8_out, EXT_MEM_CLK);
  // Probe on EXT_TEL_OPERAND
  Comparator comparator_4 (.a(EXT_TEL_OPCODE), .b({8{1'b0}}), .eq(comparator_4_eq));  // open: gt, lt
  Counter #(.max('hffff), .width(16)) counter_2 (
    .load(or_7_out), .D(multiplexer_5_out), .count(or_6_out), .Q({PC_HI[7], MEM15}), .up(1'b1), .clk(CLK),
    .clr(RST));  // open: carry
  or or_6 (or_6_out, INC_PC, or_7_out);
  ROM #(.addrWidth(15)) rom_2 (.addr(MEM15), .data(rom_2_data));
  // Probe on MEM
  assign MEM = PC_HI[7] ? ram_1_dout : 8'bz;  // Controlled_Buffer controlled_buffer_13
  or or_7 (or_7_out, PC_HI_ACC, PC_LO_ACC);
  Comparator comparator_5 (.a(EXT_MEM_OPCODE), .b({8{1'b0}}), .eq(comparator_5_eq));  // open: gt, lt
  Comparator comparator_6 (.a(EXT_MEM_OPCODE), .b(8'h1), .eq(comparator_6_eq));  // open: gt, lt
  Comparator comparator_7 (.a(EXT_MEM_OPCODE), .b(8'h2), .eq(comparator_7_eq));  // open: gt, lt
  Comparator comparator_8 (.a(EXT_MEM_OPCODE), .b(8'h3), .eq(comparator_8_eq));  // open: gt, lt
  Comparator comparator_9 (.a(EXT_MEM_OPCODE), .b(8'h4), .eq(comparator_9_eq));  // open: gt, lt
  Comparator comparator_10 (.a(EXT_MEM_OPCODE), .b(8'h69), .eq(comparator_10_eq));  // open: gt, lt
  // Probe on telnet_1_p4
  // Telnet #(.port(8080)) telnet_1: pin names not known; wires that end beside it: EXT_TEL_OPERAND, EXT_TEL_CLK, comparator_4_eq, telnet_1_p4, telnet_1_p5, PRT_C_B, telnet_1_p7
  Multiplexer #(.width(8)) multiplexer_5 (.in0(MEM15[7:0]), .in1(ACC), .out(multiplexer_5_out[7:0]), .sel(PC_LO_ACC));
  Multiplexer #(.width(8)) multiplexer_6 (
    .in0({PC_HI[7], MEM15[14:8]}), .in1(ACC), .out(multiplexer_5_out[15:8]), .sel(PC_HI_ACC));
  Register register_1 (.D(EXT_MEM_OPERAND), .en(comparator_5_eq), .clk(EXT_MEM_PRO), .Q(register_1_q));  // open: clr
  Register register_2 (.D(EXT_MEM_OPERAND), .en(comparator_6_eq), .clk(EXT_MEM_PRO), .Q(register_2_q));  // open: clr
  Register register_3 (.D(EXT_MEM_OPERAND), .en(comparator_7_eq), .clk(EXT_MEM_PRO), .Q(register_3_q));  // open: clr
  not not_9 (not_9_out, comparator_10_eq);
  assign EXT_0 = telnet_1_p7 ? telnet_1_p5 : 1'bz;  // Controlled_Buffer controlled_buffer_14
  TTL_manager ttl_manager_1 (
    .ACC(ACC), .RST(RST), .EN(PRT_A_B), .TTL_DAT(ttl_manager_1_ttl_dat), .TTL_RST(ttl_manager_1_ttl_rst),
    .TTL_EN(ttl_manager_1_ttl_en));
  not not_10 (not_10_out, PC_HI[7]);
  assign PRT_C = telnet_1_p7 ? multiplexer_7_out : 8'bz;  // Controlled_Buffer controlled_buffer_15
  Multiplexer #(.width(8)) multiplexer_7 (.in0(8'h2), .in1(telnet_1_p4), .out(multiplexer_7_out), .sel(not_9_out));
  TTY #(.cols(60), .rows(24)) tty_1 (
    .data(ttl_manager_1_ttl_dat), .clk(CLK), .we(ttl_manager_1_ttl_en), .clr(ttl_manager_1_ttl_rst));
  // Probe on MEM
  assign MEM = not_10_out ? rom_2_data : 8'bz;  // Controlled_Buffer controlled_buffer_16
  Comparator #(.mode("unsigned"), .width(2)) comparator_11 (
    .a(2'b01), .b(PRT_BC_SEL), .eq(telnet_1_p7));  // open: gt, lt
  RAM #(.addrWidth(17), .asyncread("true"), .\type ("nonvolatile")) ram_2 (
    .addr({register_3_q[0], register_2_q, register_1_q}), .we(comparator_8_eq), .oe(1'b1), .clk(EXT_MEM_PRO),
    .din(EXT_MEM_OPERAND), .dout(ram_2_dout));
  Slider #(.width(2)) slider_1 (.out(PRT_BC_SEL));
  and and_6 (and_6_out, CLK, comparator_9_eq);
  Comparator comparator_12 (.a(EXT_MEM_OPCODE), .b(8'h69), .eq(comparator_12_eq));  // open: gt, lt
  Random random_1 (.next(1'b1), .clk(and_6_out), .out(random_1_out));  // open: clr
  not not_11 (not_11_out, comparator_12_eq);
  Multiplexer #(.width(8)) multiplexer_8 (
    .in0(ram_2_dout), .in1(random_1_out), .out(multiplexer_8_out), .sel(comparator_9_eq));
  Button button_1 (.out(RST));
  Multiplexer #(.width(8)) multiplexer_9 (
    .in0(8'h1), .in1(multiplexer_8_out), .out(multiplexer_9_out), .sel(not_11_out));
  assign PRT_C = comparator_13_eq ? multiplexer_9_out : 8'bz;  // Controlled_Buffer controlled_buffer_17
  // Probe on PRT_C
  Comparator #(.mode("unsigned"), .width(2)) comparator_13 (
    .a(2'b00), .b(PRT_BC_SEL), .eq(comparator_13_eq));  // open: gt, lt
  Keyboard keyboard_1 (
    .clk(key_manager_1_con), .re(key_manager_1_rd), .clr(key_manager_1_clr), .avail(keyboard_1_avail),
    .data(keyboard_1_data));
  KEY_MANAGER key_manager_1 (
    .KEY(keyboard_1_data), .ENABLE(PRT_D_B), .CLK(CLK), .AV(keyboard_1_avail), .OPERAND(MCC_OP),
    .CON(key_manager_1_con), .RD(key_manager_1_rd), .CLR(key_manager_1_clr), .GET(PRT_D), .EXT(EXT_1));

  // Other names for the same wires on the sheet: PC_LO[7:0] = MEM15[7:0]; PC_HI[6:0] = MEM15[14:8]

  // Notes on the sheet:
  //   contents of rom_1 (hex, n*v repeats v):
  //   a0 1 c0 2 ff 0 0 0 3 e0 b0 3 e0 d0 a0 1 c0 2 ff 0 e4 b0 e5 d0 80 1 60 2 0 f0 a0 1 c0 2 3 ff e4 b0 e5
  //   d0 80 1 60 2 20 f0 a0 1 c0 2 3 ff e4 b0 e5 d0 80 1 60 2 40 f0 a0 1 c0 2 3 ff 3 e0 10 3 ff 0 0 0 3 e0
  //   30 3 ff 0 0 0 3 e0 50 3 ff 0 0 0 3 e0 70 3 ff 0 0 0 3 e0 90 3 ff 0 0 0 3 e0 b0 3 ff 0 0 0 3 e0 d0 3
  //   ff 11*0 e4 b0 e5 d0 80 1 60 2 e0 10 a0 1 c0 2 3 ff e4 b0 e5 d0 80 1 60 2 e0 30 a0 1 c0 2 3 ff e4 b0
  //   e5 d0 80 1 60 2 e0 50 a0 1 c0 2 3 ff e4 b0 e5 d0 80 1 60 2 e0 70 a0 1 c0 2 3 ff e4 b0 e5 d0 80 1 60
  //   2 e0 90 a0 1 c0 2 3 ff e4 b0 e5 d0 80 1 60 2 e0 b0 a0 1 c0 2 3 ff e4 b0 e5 d0 80 1 60 2 e0 d0 a0 1
  //   c0 2 3 ff 5*0 30 3 ff 0 50 3 ff 0 70 3 ff 0 90 3 ff 0 b0 3 ff 0 d0 3 ff 20 10 3 ff 20 50 3 ff 20 70
  //   3 ff 20 90 3 ff 20 b0 3 ff 20 d0 3 ff 40 10 3 ff 40 30 3 ff 40 70 3 ff 40 90 3 ff 40 b0 3 ff 40 d0 3
  //   ff 60 10 3 ff 60 30 3 ff 60 50 3 ff 60 90 3 ff 60 b0 3 ff 60 d0 3 ff 80 10 3 ff 80 30 3 ff 80 50 3
  //   ff 80 70 3 ff 80 b0 3 ff 80 d0 3 ff a0 10 3 ff a0 30 3 ff a0 50 3 ff a0 70 3 ff a0 90 3 ff a0 d0 3
  //   ff c0 10 3 ff c0 30 3 ff c0 50 3 ff c0 70 3 ff c0 90 3 ff c0 b0 3 ff 0 48 3 ff 20 48 3 ff 40 48 3 ff
  //   60 48 3 ff 80 48 3 ff a0 48 3 ff c0 48 3 ff 5*0 88 3 ff 20 88 3 ff 40 88 3 ff 60 88 3 ff 80 88 3 ff
  //   a0 88 3 ff c0 88 3 ff 4*0 e7 10 3 ff e7 30 3 ff e7 50 3 ff e7 70 3 ff e7 90 3 ff e7 b0 3 ff e7 d0 3
  //   ff 4*0 38 3 ff 0 28 3 ff 0 18 3 ff 0 8 3 ff 0 3 9 3 ff 3 19 3 ff 3 29 3 ff 3 39 3 ff 3 49 3 ff 3 59
  //   63 ff 3 69 3 ff 3 79 3 ff 3 89 3 ff 3 99 3 ff 3 a9 3 ff 3 b9 3 ff 3 c9 3 ff 3 d9 3 ff 3 e9 3 ff 3 f9
  //   3 ff 0 a 3 ff 20 a 3 ff 40 a 3 ff 60 a 3 ff 80 a 3 ff a0 a 3 ff c0 a 3 ff fa 3 ff 0 eb 10 3 ff eb 30
  //   3 ff eb 50 3 ff eb 70 3 ff eb 90 3 ff eb b0 3 ff eb d0 3 ff 4*0 e4 b0 e5 d0 3 e0 b0 3 e0 2 0 f0 a0 1
  //   c0 2 3 ff 0 0 e4 b0 e5 d0 3 e0 1 3 e0 2 20 f0 a0 1 c0 2 3 ff 10*0 e4 b0 e5 d0 3 e0 1 3 e0 2 40 f0 a0
  //   1 c0 2 3 ff 0 0 e4 b0 e5 d0 3 e0 1 3 e0 2 60 f0 a0 1 c0 2 3 ff 10*0 e4 b0 e5 d0 3 e0 1 3 e0 2 80 f0
  //   a0 1 c0 2 3 ff 0 0 e4 b0 e5 d0 3 e0 1 3 e0 2 a0 f0 a0 1 c0 2 3 ff 10*0 e4 b0 e5 d0 3 e0 1 3 e0 2 c0
  //   f0 a0 1 c0 2 3 ff 6*0 3 e0 48 3 ff 0 0 0 3 e0 88 3 ff 4*0 c 3 ff 20 c 3 ff 40 c 3 ff 60 c 3 ff 80 c
  //   3 ff a0 c 3 ff c0 c 3 ff 4*0 ed 10 3 ff ed 30 3 ff ed 50 3 ff ed 70 3 ff ed 90 3 ff ed b0 3 ff ed d0
  //   3 ff 4*0 ee 10 3 ff ee 30 3 ff ee 50 3 ff ee 70 3 ff ee 90 3 ff ee b0 3 ff ee d0 3 ff 4*0 1f 3 ff 0
  //   3 ff 34*0 43 72 65 61 74 65 64 20 62 79 20 4c 6f 75 69 73 20 57 68 69 74 65 20 32 30 32 36 a 19*0 ff
  //   contents of rom_2 (hex, n*v repeats v):
  //   eb eb 11 5a 94 11 65 94 11 72 94 11 6f 94 11 69 94 11 6e 94 11 67 94 11 20 94 11 72 94 11 65 94 11
  //   67 94 11 69 94 11 73 94 11 74 94 11 65 94 11 72 94 11 73 94 11 0 11 2e 94 13 0 11 2e 94 15 0 11 2e
  //   94 17 0 11 2e 94 19 0 11 2e 94 1b 0 11 2e 94 1d 0 11 2e 94 11 2e 94 11 4f 94 11 4b 94 11 a 94 11 0 2
  //   0 69 eb 11 43 94 11 68 94 11 65 94 11 63 94 11 6b 94 11 69 94 11 6e 94 11 67 94 11 20 94 11 66 94 11
  //   6f 94 11 72 94 11 20 94 11 52 94 11 41 94 11 4d 94 19 80 17 0 11 2e 94 13 1 15 0 11 55 5 68 11 2e 94
  //   21 70 8b 4b 11 2e 94 11 aa 5 68 11 2e 94 21 70 8b 4b 11 2e 94 71 6a 1b 2 1d 9f 11 2e 94 8d 0 11 2e
  //   94 11 2e 94 11 4f 94 11 4b 94 11 a 94 2 0 de eb 11 56 94 11 65 94 11 72 94 11 69 94 11 66 94 11 79
  //   94 11 69 94 11 6e 94 11 67 94 11 20 94 11 52 94 11 41 94 11 4d 94 19 80 17 0 2 1 d eb 11 55 5 68 21
  //   70 8b 4b 11 aa 5 68 21 70 8b 4b 11 0 5 71 6a 1b 2 1d 9f 8d 0 11 88 68 74 1b 1 1d 40 8b 0 11 0 68 73
  //   1b 1 1d 40 8b 0 2 1 5a eb 11 1 68 73 80 7b 1b 1 1d 50 89 0 2 1 d eb 74 80 7c 11 2e 94 2 1 d eb 11 4f
  //   94 11 4b 94 11 a 94 eb 11 49 94 11 44 94 11 69 94 11 6e 94 11 67 94 11 20 94 11 70 94 11 65 94 11 72
  //   94 11 69 94 11 70 94 11 68 94 11 65 94 11 72 94 11 61 94 11 6c 94 11 3a 94 11 20 94 11 69 d2 d2 da
  //   68 11 1 70 1b 1 1d b6 8d 0 11 2 70 1b 1 1d cc 8d 0 2 1 eb eb 11 44 94 11 72 94 11 69 94 11 76 94 11
  //   65 94 11 a 94 2 2 5e eb 11 43 94 11 6f 94 11 6d 94 11 70 94 11 75 94 11 74 94 11 65 94 11 72 94 11 a
  //   94 2 2 5e eb 11 70 94 11 65 94 11 72 94 11 69 94 11 70 94 11 68 94 11 65 94 11 72 94 11 61 94 11 6c
  //   94 11 20 94 11 6e 94 11 6f 94 11 74 94 11 20 94 11 72 94 11 65 94 11 63 94 11 6f 94 11 67 94 11 6e
  //   94 11 69 94 11 73 94 11 65 94 11 64 94 11 20 94 11 6f 94 11 72 94 11 20 94 11 6d 94 11 69 94 11 73
  //   94 11 73 94 11 69 94 11 6e 94 11 67 94 11 a 94 2 2 5e eb 11 c 94 19 10 17 0 2 2 69 eb 21 94 11 11 68
  //   74 1b 2 1d 83 8b 0 11 41 68 73 1b 2 1d 83 8b 0 2 2 9d eb 11 1 68 73 80 7b 1b 2 1d 93 89 0 2 2 69 eb
  //   74 80 7c 11 2e 94 2 2 69 eb ea eb 11 42 94 11 6f 94 11 6f 94 11 74 94 11 20 94 11 69 94 11 6e 94 11
  //   69 94 11 74 94 11 20 94 11 66 94 11 61 94 11 69 94 11 6c 94 11 a 94 ea 3378*0 7*40 5*20 5*40 20 20
  //   20 40 7*20 40 a 40 6*20 40 20 20 20 40 5*20 40 20 20 40 7*20 40 a 40 7*20 40 20 40 7*20 40 20 20 40
  //   5*20 40 a 40 7*20 40 20 40 7*20 40 20 20 20 40 20 20 20 40 a 8*40 20 20 40 7*20 40 4*20 40 40 40 a
  //   40 7*20 40 20 40 7*20 40 20 20 20 40 20 20 20 40 a 40 7*20 40 20 40 7*20 40 20 20 40 5*20 40 a 40
  //   6*20 40 20 20 20 40 5*20 40 20 20 40 7*20 40 a 7*40 5*20 5*40 20 20 20 40 7*20 40 a a 29*3d a 43 6f
  //   70 79 72 69 67 68 74 28 63 29 20 4c 6f 75 69 73 20 57 68 69 74 65 20 32 30 32 36
endmodule

module regs (
  input  EN,
  input  CLK,
  input  [7:0] VAL,
  input  [3:0] RGS,
  output WRT,
  output [7:0] REGA
);

  wire and_1_out, and_2_out, button_1_out, decoder_1_out0, decoder_1_out1, decoder_1_out2, decoder_1_out3,
       decoder_1_out4, decoder_1_out5, decoder_1_out6, not_1_out;
  wire [7:0] multiplexer_1_out, register_1_q, register_2_q, register_3_q, register_4_q, register_5_q,
       register_6_q, register_7_q;

  and and_1 (and_1_out, EN, RGS[0]);
  Decoder #(.select(3)) decoder_1 (
    .out0(decoder_1_out0), .out1(decoder_1_out1), .out2(decoder_1_out2), .out3(decoder_1_out3),
    .out4(decoder_1_out4), .out5(decoder_1_out5), .out6(decoder_1_out6), .out7(WRT), .sel(RGS[3:1]),
    .en(and_1_out));
  Register register_1 (.D(REGA), .en(decoder_1_out0), .clk(CLK), .Q(register_1_q), .clr(button_1_out));
  Register register_2 (.D(REGA), .en(decoder_1_out1), .clk(CLK), .Q(register_2_q), .clr(button_1_out));
  Register register_3 (.D(REGA), .en(decoder_1_out2), .clk(CLK), .Q(register_3_q), .clr(button_1_out));
  Register register_4 (.D(REGA), .en(decoder_1_out3), .clk(CLK), .Q(register_4_q), .clr(button_1_out));
  Register register_5 (.D(REGA), .en(decoder_1_out4), .clk(CLK), .Q(register_5_q), .clr(button_1_out));
  Register register_6 (.D(REGA), .en(decoder_1_out5), .clk(CLK), .Q(register_6_q), .clr(button_1_out));
  Register register_7 (.D(REGA), .en(decoder_1_out6), .clk(CLK), .Q(register_7_q), .clr(button_1_out));
  Multiplexer #(.select(3), .width(8)) multiplexer_1 (
    .in0(register_1_q), .in1(register_2_q), .in2(register_3_q), .in3(register_4_q), .in4(register_5_q),
    .in5(register_6_q), .in6(register_7_q), .in7(VAL), .out(multiplexer_1_out), .sel(RGS[3:1]));
  Button button_1 (.out(button_1_out));
  not not_1 (not_1_out, RGS[0]);
  and and_2 (and_2_out, EN, not_1_out);
  Register register_8 (.D(multiplexer_1_out), .en(and_2_out), .clk(CLK), .Q(REGA), .clr(button_1_out));

  // Other names for the same wires on the sheet: DAT[2:0] = RGS[3:1]
endmodule

module alu_flags (
  input  CLK,
  input  EN,
  input  [7:0] INP,
  input  [3:0] SEL,
  output [7:0] SHI,
  output GRE,
  output EQU,
  output LES,
  output ZER,
  output [7:0] RES,
  output CAR
);

  wire adder_1_cout, and_1_out, and_2_out, decoder_1_out1, decoder_1_out2, decoder_2_out0, decoder_2_out1,
       decoder_2_out2, decoder_2_out3, not_1_out, not_2_out, not_3_out, not_4_out, not_5_out, not_6_out,
       not_7_out, not_8_out, or_1_out, or_2_out, subtractor_1_bout;
  wire [1:0] SEL_t;
  wire [3:0] shifter_1_out;
  wire [7:0] adder_1_out, divider_1_out, divider_1_rem, IN1, IN2, multiplier_1_cout, multiplier_1_out,
       subtractor_1_out;

  Adder adder_1 (.a(IN1), .b(IN2), .out(adder_1_out), .cout(adder_1_cout));  // open: cin
  assign CAR = decoder_2_out3 ? adder_1_cout : 1'bz;  // Controlled_Buffer controlled_buffer_1
  Decoder #(.select(2)) decoder_1 (
    .out1(decoder_1_out1), .out2(decoder_1_out2), .sel(SEL[3:2]));  // open: out0, out3, en
  Register #(.width(2)) register_1 (.D(SEL[1:0]), .en(EN), .clk(CLK), .Q(SEL_t));  // open: clr
  Decoder #(.select(2)) decoder_2 (
    .out0(decoder_2_out0), .out1(decoder_2_out1), .out2(decoder_2_out2), .out3(decoder_2_out3), .sel(SEL_t));  // open: en
  Subtractor subtractor_1 (.a(IN1), .b(IN2), .out(subtractor_1_out), .bout(subtractor_1_bout));  // open: bin
  assign CAR = decoder_2_out2 ? subtractor_1_bout : 1'bz;  // Controlled_Buffer controlled_buffer_2
  Register register_2 (.D(INP), .en(decoder_1_out1), .clk(and_1_out), .Q(IN1));  // open: clr
  and and_1 (and_1_out, CLK, EN);
  // Probe on IN1
  Multiplier multiplier_1 (.a(IN1), .b(IN2), .out(multiplier_1_out), .cout(multiplier_1_cout));  // open: cin
  or or_1 (or_1_out, multiplier_1_cout[7], multiplier_1_cout[6], multiplier_1_cout[5], multiplier_1_cout[4], multiplier_1_cout[3], multiplier_1_cout[2], multiplier_1_cout[1], multiplier_1_cout[0]);
  assign CAR = decoder_2_out1 ? or_1_out : 1'bz;  // Controlled_Buffer controlled_buffer_3
  Pull_Resistor pull_resistor_1 (.node(CAR));
  Register register_3 (.D(INP), .en(decoder_1_out2), .clk(and_2_out), .Q(IN2));  // open: clr
  and and_2 (and_2_out, CLK, EN);
  Divider divider_1 (.a(IN1), .b(IN2), .out(divider_1_out), .rem(divider_1_rem));  // open: upper
  or or_2 (or_2_out, divider_1_rem[7], divider_1_rem[6], divider_1_rem[5], divider_1_rem[4], divider_1_rem[3], divider_1_rem[2], divider_1_rem[1], divider_1_rem[0]);
  assign CAR = decoder_2_out0 ? or_2_out : 1'bz;  // Controlled_Buffer controlled_buffer_4
  // Probe on IN2
  Pull_Resistor pull_resistor_2 (.node(GRE));
  Pull_Resistor pull_resistor_3 (.node(EQU));
  Comparator #(.mode("unsigned")) comparator_1 (.a(IN2), .b(IN1), .gt(GRE), .eq(EQU), .lt(LES));
  not not_1 (not_1_out, RES[4]);
  not not_2 (not_2_out, RES[5]);
  not not_3 (not_3_out, RES[6]);
  not not_4 (not_4_out, RES[7]);
  Multiplexer #(.select(2), .width(8)) multiplexer_1 (
    .in0(divider_1_out), .in1(multiplier_1_out), .in2(subtractor_1_out), .in3(adder_1_out), .out(RES),
    .sel(SEL_t));
  Pull_Resistor pull_resistor_4 (.node(LES));
  Shifter shifter_1 (.in(IN1), .\dist (IN2[2:0]), .out({SHI[3:0], shifter_1_out}));
  not not_5 (not_5_out, RES[0]);
  not not_6 (not_6_out, RES[1]);
  not not_7 (not_7_out, RES[2]);
  not not_8 (not_8_out, RES[3]);
  and and_3 (ZER, not_5_out, not_6_out, not_7_out, not_8_out, not_1_out, not_2_out, not_3_out, not_4_out);

  assign SHI[7:4] = 4'b0000;

  // Other names for the same wires on the sheet: V1[7:0] = INP
endmodule

module TTL_manager (
  input  [7:0] ACC,
  input  RST,
  input  EN,
  output [6:0] TTL_DAT,
  output TTL_RST,
  output TTL_EN
);

  wire and_1_out, comparator_1_eq;

  Comparator comparator_1 (.a(ACC), .b(8'hc), .eq(comparator_1_eq));  // open: gt, lt
  and and_1 (and_1_out, comparator_1_eq, EN);
  or or_1 (TTL_RST, and_1_out, RST);

  assign TTL_DAT = ACC[6:0];
  assign TTL_EN = EN;
endmodule

module KEY_MANAGER (
  input  [6:0] KEY,
  input  ENABLE,
  input  CLK,
  input  AV,
  input  [3:0] OPERAND,
  output CON,
  output RD,
  output CLR,
  output [7:0] GET,
  output EXT
);

  wire comparator_1_eq;

  and and_1 (CLR, ENABLE, comparator_1_eq);
  Comparator #(.mode("unsigned"), .width(4)) comparator_1 (
    .a(OPERAND), .b(4'b0001), .eq(comparator_1_eq));  // open: gt, lt

  assign CON = CLK;
  assign EXT = AV;
  assign GET = {1'b0, KEY};
  assign RD = ENABLE;
endmodule
